# Fritzing sketch circuit (saved by Fritzing 0.8.7b)

parts:
  Load_Cell1 = Load Cell - Red/white/black/green
  Part1 = HX711 Weighing Sensor Module
  Part4 = Arduino Uno (Rev3)
  J3 = Basic Servo
  J4 = Basic Servo
  R5 = Resistor [tolerance=±5% resistance=330 package=THT]
  R6 = Resistor [tolerance=±5% resistance=330 package=THT]
  Part5 = SRF05 Ultrasonic Rangefinder
  Display2 = LCD screen 16x2 IIC [part_number=101290]
  S2 = Pushbutton [package="[THT]"]
  LED2 = LED - 5mm [color="Red (633nm)" package="5 mm [THT]"]

nets:
  N1: Load_Cell1.wire1, Part1.E+
  N2: Load_Cell1.wire2, Part1.A+
  N3: Load_Cell1.wire3, Part1.E-
  N4: Load_Cell1.wire4, Part1.A-
  N5: Part1.VCC, R5.Pin_0, LED2.anode
  GND: Part1.GND, Part4.GND, J3.gnd, J4.gnd, R6.Pin_1, Part5.GND, Display2.GND
  N6: Part1.DO/RX, Part4.D4
  N7: Part1.CK/TX, Part4.D5_PWM
  N8: Part4.A4/SDA, Display2.SDA
  N9: Part4.A5/SCL, Display2.SCL
  N10: Part4.D9_PWM, J3.pulse
  N11: Part4.D10_PWM/SS, J4.pulse
  N12: Part4.D12/MISO, R6.Pin_0, S2.Pin_3, S2.Pin_4
  N13: Part4.D13/SCK, LED2.cathode
  N14: Part4.D2, Part5.Trig
  N15: Part4.D3_PWM, Part5.Echo
  VCC: Part4.5V, J3.vcc, J4.vcc, R5.Pin_1, Part5.VCC, Display2.VCC, S2.Pin_1, S2.Pin_2

custom parts:
  Load Cell - Red/white/black/green: A rectangle load cell/weighting pressure Sensor with four wires - Red, white, black, green. Normally corresponding with E+, E-, A+, A- respectively.
  HX711 Weighing Sensor Module: HX711 is a precision 24-bit analog-to-digital converter (ADC) designed for weigh scales and industrial control applications to interface directly with a bridge sensor.
  LCD screen 16x2 IIC: LCD screen with HD44780 controller enables showing text, symbols, value or anything else that comes from Croduino/Arduino. It is capable of showing 16 symbols in two lines and therefore can be used in many projects that need to send clearly visible and legible output information.. • Color of symbols: White • Backlight: Blue • Dimensions: 80 x 36 x 12 mm • Screen dimensions: 64.5 x 16 mm •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
