# Fritzing sketch fish-counter-circuit (saved by Fritzing 0.8.7b)

parts:
  Part8 = Arduino Uno (Rev3)
  J3 = Basic Servo
  J4 = Basic Servo
  R5 = Resistor [tolerance=±5% resistance=330 package=THT]
  R6 = Resistor [tolerance=±5% resistance=330 package=THT]
  Load_Cell4 = Load Cell - Red/white/black/green
  Part9 = HX711 Weighing Sensor Module
  Part10 = SRF05 Ultrasonic Rangefinder
  Display2 = LCD screen 16x2 IIC [part_number=101290]
  S2 = Pushbutton [package="[THT]"]
  LED2 = LED - 5mm [color="Red (633nm)" package="5 mm [THT]"]

nets:
  N1: Part8.A3, LED2.cathode
  N2: Part8.A4/SDA, Display2.SDA
  N3: Part8.A5/SCL, Display2.SCL
  N4: Part8.D9_PWM, J3.pulse
  N5: Part8.D10_PWM/SS, J4.pulse
  N6: Part8.D11_PWM/MOSI, Part9.CK/TX
  N7: Part8.D12/MISO, Part9.DO/RX
  N8: Part8.D13/SCK, R6.Pin_0, S2.Pin_3, S2.Pin_4
  GND: Part8.GND, J3.gnd, J4.gnd, R6.Pin_1, Part9.GND, Part10.GND, Display2.GND
  N9: Part8.D2, Part10.Trig
  N10: Part8.D3_PWM, Part10.Echo
  VCC: Part8.5V, J3.vcc, J4.vcc, R5.Pin_1, Part9.VCC, Part10.VCC, Display2.VCC, S2.Pin_1, S2.Pin_2
  N11: R5.Pin_0, LED2.anode
  N12: Load_Cell4.wire1, Part9.E+
  N13: Load_Cell4.wire2, Part9.A+
  N14: Load_Cell4.wire3, Part9.E-
  N15: Load_Cell4.wire4, Part9.A-

custom parts:
  Load Cell - Red/white/black/green: A rectangle load cell/weighting pressure Sensor with four wires - Red, white, black, green. Normally corresponding with E+, E-, A+, A- respectively.
  HX711 Weighing Sensor Module: HX711 is a precision 24-bit analog-to-digital converter (ADC) designed for weigh scales and industrial control applications to interface directly with a bridge sensor.
  LCD screen 16x2 IIC: LCD screen with HD44780 controller enables showing text, symbols, value or anything else that comes from Croduino/Arduino. It is capable of showing 16 symbols in two lines and therefore can be used in many projects that need to send clearly visible and legible output information.. • Color of symbols: White • Backlight: Blue • Dimensions: 80 x 36 x 12 mm • Screen dimensions: 64.5 x 16 mm •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
